// Logisim project carrylookahead.circ as structural Verilog: 1 circuit, main circuit main
module main (
  input  C0,
  input  X0,
  input  Y0,
  input  X1,
  input  Y1,
  input  X2,
  input  Y2,
  input  X3,
  input  Y3,
  output S0,
  output C1,
  output out_12,
  output C2,
  output out_14,
  output C3,
  output out_16,
  output C4
);

  wire and_1_out, and_2_out, and_3_out, and_4_out, and_5_out, and_6_out, and_7_out, and_8_out, and_9_out,
       and_10_out, and_11_out, and_12_out, and_13_out, and_14_out, xor_1_out, xor_2_out, xor_3_out, xor_4_out;

  Hex_Digit_Display hex_digit_display_1 (.value({X3, X2, X1, X0}));  // open: dp
  Hex_Digit_Display hex_digit_display_2 (.value({Y3, Y2, Y1, Y0}));  // open: dp
  and and_1 (and_1_out, X0, Y0);
  and and_2 (and_2_out, X1, Y1);
  and and_3 (and_3_out, X2, Y2);
  and and_4 (and_4_out, X3, Y3);
  xor xor_1 (xor_1_out, X0, Y0);
  xor xor_2 (xor_2_out, X1, Y1);
  xor xor_3 (xor_3_out, X2, Y2);
  xor xor_4 (xor_4_out, X3, Y3);
  and and_5 (and_5_out, C0, xor_1_out);
  and and_6 (and_6_out, C0, xor_1_out, xor_2_out);
  and and_7 (and_7_out, and_1_out, xor_2_out);
  and and_8 (and_8_out, and_2_out, xor_3_out);
  and and_9 (and_9_out, and_1_out, xor_2_out, xor_3_out);
  and and_10 (and_10_out, xor_3_out, xor_4_out);
  and and_11 (and_11_out, and_2_out, xor_3_out, xor_4_out);
  and and_12 (and_12_out, and_1_out, xor_2_out, xor_3_out, xor_4_out);
  and and_13 (and_13_out, C0, xor_1_out, xor_2_out, xor_3_out, xor_4_out);
  and and_14 (and_14_out, C0, xor_1_out, xor_2_out, xor_3_out);
  or or_1 (C1, and_5_out, and_1_out);
  or or_2 (C2, and_6_out, and_7_out, and_2_out);
  or or_3 (C3, and_8_out, and_9_out, and_14_out, and_3_out);
  xor xor_5 (S0, xor_1_out, C0);
  xor xor_6 (out_12, C1, xor_2_out);
  xor xor_7 (out_14, C2, xor_3_out);
  xor xor_8 (out_16, C3, xor_4_out);
  or or_4 (C4, and_10_out, and_11_out, and_4_out, and_12_out, and_13_out);
  Hex_Digit_Display hex_digit_display_3 (.value({out_16, out_14, out_12, S0}));  // open: dp
endmodule
