// Logisim project universal.circ as structural Verilog: 1 circuit, main circuit main
module main (
  input  in_1,
  input  in_2,
  input  in_3,
  input  in_4,
  input  in_5,
  input  in_6,
  input  [1:0] in_7,
  input  in_8,
  input  in_9,
  output [3:0] out_10
);

  wire clock_1_out, multiplexer_1_out, multiplexer_2_out, multiplexer_3_out, multiplexer_4_out;

  Clock #(.highDuration(3), .lowDuration(3)) clock_1 (.out(clock_1_out));
  Multiplexer #(.select(2)) multiplexer_1 (
    .in0(in_5), .in1(out_10[1]), .in2(in_1), .in3(out_10[0]), .out(multiplexer_1_out), .sel(in_7));
  D_Flip_Flop d_ff_1 (
    .D(multiplexer_1_out), .clk(clock_1_out), .Q(out_10[0]), .preset(in_8), .reset(in_9));  // open: Qn
  Multiplexer #(.select(2)) multiplexer_2 (
    .in0(out_10[0]), .in1(out_10[2]), .in2(in_2), .in3(out_10[1]), .out(multiplexer_2_out), .sel(in_7));
  D_Flip_Flop d_ff_2 (
    .D(multiplexer_2_out), .clk(clock_1_out), .Q(out_10[1]), .preset(in_8), .reset(in_9));  // open: Qn
  Multiplexer #(.select(2)) multiplexer_3 (
    .in0(out_10[1]), .in1(out_10[3]), .in2(in_3), .in3(out_10[2]), .out(multiplexer_3_out), .sel(in_7));
  D_Flip_Flop d_ff_3 (
    .D(multiplexer_3_out), .clk(clock_1_out), .Q(out_10[2]), .preset(in_8), .reset(in_9));  // open: Qn
  Multiplexer #(.select(2)) multiplexer_4 (
    .in0(out_10[2]), .in1(in_6), .in2(in_4), .in3(out_10[3]), .out(multiplexer_4_out), .sel(in_7));
  D_Flip_Flop d_ff_4 (
    .D(multiplexer_4_out), .clk(clock_1_out), .Q(out_10[3]), .preset(in_8), .reset(in_9));  // open: Qn
endmodule
